# Fritzing sketch fsae_combustao (saved by Fritzing 0.9.2b)
circuit board: 20cm x 20cm

parts:
  Componente1 = Arduino Mega 2560 (Rev3)
  Componente2 = LC Studio SD Card Module
  GY1 = MPU-6050 Board GY-521 [form="♀ (female)" package=THT]
  U1 = U-Blox Neo 6M [package="NEO 6M"]

nets:
  N1: Componente1.D21/SCL, Componente1.SCL, GY1.pin3
  N2: Componente1.D20/SDA, Componente1.SDA, GY1.pin4
  N3: Componente1.D19/RX1, U1.TX-O
  N4: Componente1.D18/TX1, U1.RX-I
  N5: Componente1.D50, Componente2.MISO
  N6: Componente1.D51, Componente2.MOSI
  N7: Componente1.D52, Componente2.SCK
  N8: Componente1.D53, Componente2.CS
  N9: GY1.pin1, U1.VCC

custom parts:
  LC Studio SD Card Module: The LC Studio SD card module serves as an interface to an SD card. The module works at 3.3 volts and 5 volts. The SPI (Serial Peripheral Interface) protocol is used for communicating with the module.
  MPU-6050 Board GY-521: Acelerometro y Giroscopio MPU-6050 Board GY-521
